// Digital circuit ALU.dig as structural Verilog
module ALU (
  input  [31:0] A,
  input  [31:0] B,
  input  [3:0] F,
  output [31:0] Result
);

  wire and_2_out, and_3_out, and_4_out, comparator_1_eq, comparator_1_gt, comparator_1_lt, or_2_out;
  wire [0:0] or_3_out;
  wire [31:0] add_1_s, and_1_out, barrelshifter_1_out, barrelshifter_2_out, barrelshifter_3_out, div_1_q,
       multiplexer_1_out, multiplexer_2_out, neg_1_out, not_1_out, or_1_out, sub_1_s;
  wire [63:0] mul_1_mul;

  assign and_1_out = A & B;  // And and_1, 32 bits wide
  assign or_1_out = A | B;  // Or or_1, 32 bits wide
  assign not_1_out = ~A;  // Not not_1, 32 bits wide
  BarrelShifter #(.Bits(32), .barrelSigned("true")) barrelshifter_1 (.in(A), .shift(B[6:0]), .out(barrelshifter_1_out));
  BarrelShifter #(.Bits(32), .barrelSigned("true"), .direction("right")) barrelshifter_2 (
    .in(A), .shift(B[6:0]), .out(barrelshifter_2_out));
  BarrelShifter #(.barrelShifterMode("arithmetic"), .Bits(32), .barrelSigned("true"), .direction("right")) barrelshifter_3 (
    .in(A), .shift(B[6:0]), .out(barrelshifter_3_out));
  Neg #(.Bits(32)) neg_1 (.in(A), .out(neg_1_out));
  Add #(.Bits(32)) add_1 (.a(A), .b(B), .c_i(1'b0), .s(add_1_s));  // open: c_o
  Sub #(.Bits(32)) sub_1 (.a(A), .b(B), .c_i(1'b0), .s(sub_1_s));  // open: c_o
  Mul #(.Signed("true"), .Bits(32)) mul_1 (.a(A), .b(B), .mul(mul_1_mul));
  Div #(.Signed("true"), .Bits(32)) div_1 (.a(A), .b(B), .q(div_1_q));  // open: r
  Comparator #(.Signed("true"), .Bits(32)) comparator_1 (
    .a(A), .b({32{1'b0}}), .gt(comparator_1_gt), .eq(comparator_1_eq), .lt(comparator_1_lt));
  and and_2 (and_2_out, comparator_1_gt, B[2]);
  and and_3 (and_3_out, comparator_1_eq, B[1]);
  and and_4 (and_4_out, comparator_1_lt, B[0]);
  or or_2 (or_2_out, comparator_1_gt, comparator_1_lt);
  Multiplexer #(.Bits(32)) multiplexer_1 (.sel(or_2_out), .in_0({32{1'b0}}), .in_1(32'h1), .out(multiplexer_1_out));
  Multiplexer #(.Bits(32)) multiplexer_2 (
    .sel(comparator_1_eq), .in_0({32{1'b0}}), .in_1(32'h1), .out(multiplexer_2_out));
  or or_3 (or_3_out[0], and_2_out, and_3_out, and_4_out);
  Multiplexer #(.Selector_Bits(4), .Bits(32)) multiplexer_3 (
    .sel(F), .in_0(A), .in_1(B), .in_2(and_1_out), .in_3(or_1_out), .in_4(not_1_out),
    .in_5(barrelshifter_1_out), .in_6(barrelshifter_2_out), .in_7(barrelshifter_3_out), .in_8(neg_1_out),
    .in_9(add_1_s), .in_10(sub_1_s), .in_11(mul_1_mul[31:0]), .in_12(div_1_q), .in_13(multiplexer_1_out),
    .in_14(multiplexer_2_out), .in_15({{31{1'b0}}, or_3_out[0]}), .out(Result));
endmodule
