// Digital circuit ControlUnit.dig as structural Verilog
module ControlUnit (
  input  [31:0] Mem_In,
  input  [31:0] PC_In,
  input  CLK,
  input  [2:0] PZN,
  input  PC_Write,
  input  [31:0] PD_In,
  input  PD_Write,
  output [5:0] Device,
  output [15:0] Address,
  output [31:0] PC_Out,
  output [31:0] PD_Out,
  output [31:0] Next_Line,
  output [27:0] Instr,
  output [31:0] Constant
);

  wire comparator_1_eq, delay_1_out, fetchunit_1_start_execute, or_1_out, reset_1_out;
  wire [2:0] sid_1_p8, sid_1_p9;
  wire [5:0] multiplexer_2_out, multiplexer_4_out;
  wire [15:0] multiplexer_1_out, multiplexer_3_out, nextstate_1_next_state, register_1_q, sid_1_p1, sid_1_p6,
       sid_1_p7;
  wire [31:0] fetchunit_1_instruction;
  wire [63:16] sid_1_p4;

  Reset #(.invertOutput("false")) reset_1 (.out(reset_1_out));
  Multiplexer #(.Bits(16)) multiplexer_1 (.sel(PC_Write), .in_0(sid_1_p6), .in_1(PC_In[15:0]), .out(multiplexer_1_out));
  Delay #(.delayTime(2)) delay_1 (.in(reset_1_out), .out(delay_1_out));
  Multiplexer #(.Bits(6)) multiplexer_2 (
    .sel(PD_Write), .in_0(PD_Out[5:0]), .in_1(PD_In[5:0]), .out(multiplexer_2_out));
  or or_1 (or_1_out, CLK, reset_1_out);
  FetchUnit fetchunit_1 (
    .CLK(CLK), .Start(comparator_1_eq), .PD(PD_Out[5:0]), .PC(PC_Out[15:0]), .Mem_In(Mem_In),
    .Start_Execute(fetchunit_1_start_execute), .Device(Device), .Addr(Address),
    .Instruction(fetchunit_1_instruction), .Next_Line(Next_Line));
  Multiplexer #(.Bits(16)) multiplexer_3 (
    .sel(delay_1_out), .in_0(multiplexer_1_out), .in_1({16{1'b0}}), .out(multiplexer_3_out));
  Multiplexer #(.Bits(6)) multiplexer_4 (
    .sel(delay_1_out), .in_0(multiplexer_2_out), .in_1(6'b000010), .out(multiplexer_4_out));
  Register #(.Bits(16)) PC (.D(multiplexer_3_out), .C(~or_1_out), .en(1'b1), .Q(PC_Out[15:0]));
  Register #(.Bits(6)) PD (.D(multiplexer_4_out), .C(~or_1_out), .en(1'b1), .Q(PD_Out[5:0]));
  // SID sid_1: pin names not known; wires that end beside it: sid_1_p1, sid_1_p4[62:60], PZN, {sid_1_p4[63:60], Instr, sid_1_p4[31:16], Constant[15:0]}, PC_Out[15:0], sid_1_p6, sid_1_p7, sid_1_p8, sid_1_p9
  // Probe External PC on PC_Out[15:0]
  // Probe External PD on PD_Out[5:0]
  NextState nextstate_1 (
    .Start_Execute(fetchunit_1_start_execute), .Instruction(fetchunit_1_instruction),
    .Prev__State(register_1_q), .Branch_Loc(sid_1_p7), .Branch_Cond(sid_1_p8), .PZN(sid_1_p9),
    .Next_State(nextstate_1_next_state));
  Register #(.Bits(16)) register_1 (.D(nextstate_1_next_state), .C(CLK), .en(1'b1), .Q(register_1_q));
  Comparator #(.Bits(16)) comparator_1 (.a(register_1_q), .b({16{1'b0}}), .eq(comparator_1_eq));  // open: gt, lt
  ROM #(.AddrBits(16), .Bits(64)) rom_1 (
    .A(register_1_q), .sel(1'b1), .D({sid_1_p4[63:60], Instr, sid_1_p4[31:16], Constant[15:0]}));
  // Probe Internal PC on register_1_q
  // Probe Instruction on {sid_1_p4[63:60], Instr, sid_1_p4[31:16], Constant[15:0]}
  Multiplexer #(.Bits(16)) multiplexer_5 (
    .sel(sid_1_p4[63]), .in_0(Constant[15:0]), .in_1(sid_1_p4[31:16]), .out(sid_1_p1));
  Multiplexer #(.Bits(16)) multiplexer_6 (
    .sel(sid_1_p4[63]), .in_0(sid_1_p4[31:16]), .in_1({16{1'b0}}), .out(Constant[31:16]));

  assign PC_Out[31:16] = {16{1'b0}};
  assign PD_Out[31:6] = {26{1'b0}};

  // Notes on the sheet:
  //   contents of rom_1 (hex, n*v repeats v):
  //   0,0,0,0,0,0,0,0,0,0,0,0,0,0,0,0,888088000000006,2280000000000013,7a22a00000000012,
  //   888a00000000001,880018000000006,888900000000010,808088000000000,8892000ffff0000,989600000000010,
  //   88820000000ffff,880018000000004,980018000000005,1,0,0,0,800060000000000,2,0,0,0,0,
  //   0,0,0,0,0,0,0,0,0,0,8000c0000000000,1,0,0,0,0,0,0,0,0,0,0,0,0,0,0,8080c0000000000,
  //   8090c0000000000,810920000000000,1,0,0,0,0,0,0,0,0,0,0,0,0,8080c0000000000,8090c0000000000,
  //   810a20000000000,1,0,0,0,0,0,0,0,0,0,0,0,0,8080c0000000000,8090c0000000000,810b20000000000,
  //   1,0,0,0,0,0,0,0,0,0,0,0,0,8080c0000000000,8090c0000000000,810c20000000000,1,0,0,0,
  //   0,0,0,0,0,0,0,0,0,8080c0000000000,800820000000000,1,0,0,0,0,0,0,0,0,0,0,0,0,0,b888088000900007,
  //   8880b8000000002,1,0,0,0,0,0,0,0,0,0,0,0,0,0,8800d8000000003,1,0,0,0,0,0,0,0,0,0,0,
  //   0,0,0,0,8080c0000000000,8000c4000000000,808080000000000,880018000000003,1,0,0,0,0,
  //   0,0,0,0,0,0,0,8080c0000000000,8090c0000000000,80a0c0000000000,989500000000008,818300000000000,
  //   a00a28400000000,1,0,0,0,0,0,0,0,0,0,8080c0000000000,8000c4000000000,808080000000000,
  //   800020000000000,1,0,0,0,0,0,0,0,0,0,0,0,8080c0000000000,8000c4000000000,8090c0000000000,
  //   900010000000000,1,0,0,0,0,0,0,0,0,0,0,0,8080c0000000000,8090c0000000000,818a00000000000,
  //   809080000000000,810f20000000000,2,0,0,0,0,0,0,0,0,0,0,8080c0000000000,58090c0000000103,
  //   1,880018000000004,0,0,0,0,0,0,0,0,0,0,0,0,8080c0000000000,8090c0000000000,580a0c0000000114,
  //   1,88a088000000004,88b088000000005,b8b500000000010,a3a300000000000,88b088000000006,
  //   b8b900000000010,a30018000000000,b8ba0000000000f,b80018000000006,880018000000004,980018000000005,
  //   0,8080c0000000000,8090c0000000000,800020000000000,900020000000000,1,0,0,0,0,0,0,0,
  //   0,0,0,0,8080c0000000000,8090c0000000000,810220000000000,1,0,0,0,0,0,0,0,0,0,0,0,0,
  //   8080c0000000000,8090c0000000000,810320000000000,1,0,0,0,0,0,0,0,0,0,0,0,0,8080c0000000000,
  //   800820000000000,1,0,0,0,0,0,0,0,0,0,0,0,0,0,8080c0000000000,8090c0000000000,810520000000000,
  //   1,0,0,0,0,0,0,0,0,0,0,0,0,8080c0000000000,8090c0000000000,810620000000000,1,0,0,0,
  //   0,0,0,0,0,0,0,0,0,8080c0000000000,8090c0000000000,810220000000000,1,0,0,0,0,0,0,0,
  //   0,0,0,0,0,8080c0000000000,8090c0000000000,989500000000008,818300000000000,8090c0000000000,
  //   819088500000000,98a600000000018,98b600000000010,b8b2000000000ff,98920000000ffff,88c100000000000,
  //   88d100000000000,90e000000000000,86f081500000000,f00011400000000,70000000000001a1,
  //   1,e8e900000000001,888900000000001,c8c900000000001,4c20a0000000019d,e2ea00000000000,
  //   e8e900000000100,88c100000000000,d8d900000000001,4d30a0000000019d,1
endmodule
