// Digital circuit Debugger.dig as structural Verilog
module Debugger (
  input  [31:0] PC,
  input  Enable,
  input  Step,
  input  CLK,
  output D_CLK
);

  wire and_1_out, and_2_out, comparator_1_gt, comparator_1_lt, d_ff_1_q, d_ff_2_nq, or_1_out, or_2_out;
  wire [31:0] register_1_q;

  or or_1 (or_1_out, d_ff_1_q, ~or_2_out);  // Or
  Register #(.Bits(32)) register_1 (.D(PC), .C(CLK), .en(or_1_out), .Q(register_1_q));
  D_FF d_ff_1 (.D(Step), .C(CLK), .Q(d_ff_1_q));  // open: nQ
  D_FF d_ff_2 (.D(d_ff_1_q), .C(CLK), .nQ(d_ff_2_nq));  // open: Q
  Comparator #(.Bits(32)) comparator_1 (
    .a(PC), .b(register_1_q), .gt(comparator_1_gt), .lt(comparator_1_lt));  // open: eq
  or or_2 (or_2_out, comparator_1_gt, comparator_1_lt);
  and and_1 (and_1_out, d_ff_1_q, d_ff_2_nq);
  and and_2 (and_2_out, or_2_out, ~and_1_out, Enable);  // And
  Multiplexer multiplexer_1 (.sel(and_2_out), .in_0(CLK), .in_1(1'b0), .out(D_CLK));
endmodule
