// Digital circuit Device0.dig as structural Verilog
module Device0 (
  input  [15:0] Addr,
  input  [31:0] Data_In,
  input  Write,
  input  [31:0] Stack_Top,
  input  [15:0] Stack_Pointer,
  input  CLK,
  input  [31:0] PC_In,
  input  [31:0] PD_In,
  input  [5:0] Select,
  output [31:0] Data,
  output PC_Write,
  output PD_Write,
  output [15:0] New_Pointer,
  output Write_Pointer
);

  wire and_1_out, and_2_out, comparator_1_eq, comparator_2_gt, demultiplexer_1_out_0, demultiplexer_1_out_2,
       demultiplexer_1_out_3, demultiplexer_1_out_6, demultiplexer_1_out_8, demultiplexer_1_out_9,
       demultiplexer_1_out_10, demultiplexer_1_out_11, demultiplexer_1_out_12, demultiplexer_1_out_13,
       demultiplexer_1_out_14, demultiplexer_1_out_15;
  wire [0:0] keyboardbuffer_1_p6;
  wire [15:0] add_1_s;
  wire [31:0] keyboardbuffer_1_p5, multiplexer_1_out, multiplexer_2_out, register_1_q, register_2_q,
       register_3_q, register_4_q, register_5_q, register_6_q, register_7_q, sounddevice_1_q, SUB_POINTER_q,
       Subroutine_Stack_d, USER_OUT_q;

  Comparator #(.Bits(6)) comparator_1 (.a(Select), .b({6{1'b0}}), .eq(comparator_1_eq));  // open: gt, lt
  Comparator #(.Bits(16)) comparator_2 (.a(Addr), .b(16'ha), .gt(comparator_2_gt));  // open: eq, lt
  Add #(.Bits(16)) add_1 (.a(Addr), .b(16'ha), .c_i(1'b0), .s(add_1_s));  // open: c_o
  and and_1 (and_1_out, comparator_1_eq, Write);
  and and_2 (and_2_out, comparator_2_gt, comparator_1_eq);
  Demultiplexer #(.Selector_Bits(4)) demultiplexer_1 (
    .sel(Addr[3:0]), .in(and_1_out), .out_0(demultiplexer_1_out_0), .out_1(Write_Pointer),
    .out_2(demultiplexer_1_out_2), .out_3(demultiplexer_1_out_3), .out_4(PC_Write), .out_5(PD_Write),
    .out_6(demultiplexer_1_out_6), .out_8(demultiplexer_1_out_8), .out_9(demultiplexer_1_out_9),
    .out_10(demultiplexer_1_out_10), .out_11(demultiplexer_1_out_11), .out_12(demultiplexer_1_out_12),
    .out_13(demultiplexer_1_out_13), .out_14(demultiplexer_1_out_14), .out_15(demultiplexer_1_out_15));  // open: out_7
  BlockRAMDualPort #(.AddrBits(16), .Bits(32)) Subroutine_Stack (
    .A(add_1_s), .Din(Data_In), .str(and_2_out), .C(CLK), .D(Subroutine_Stack_d));
  PullDown pulldown_1 (.out(demultiplexer_1_out_0));
  // KeyboardBuffer keyboardbuffer_1: pin names not known; wires that end beside it: CLK, Addr[3:0], comparator_1_eq, demultiplexer_1_out_2, keyboardbuffer_1_p5, keyboardbuffer_1_p6[0]
  Terminal #(.termWidth(128)) terminal_1 (.D(Data_In), .C(CLK), .en(demultiplexer_1_out_3));
  Register #(.Bits(32)) SUB_POINTER (.D(Data_In), .C(CLK), .en(demultiplexer_1_out_6), .Q(SUB_POINTER_q));
  Register #(.Bits(32)) register_1 (.D(Data_In), .C(CLK), .en(demultiplexer_1_out_10), .Q(register_1_q));
  Register #(.Bits(32)) register_2 (.D(Data_In), .C(CLK), .en(demultiplexer_1_out_13), .Q(register_2_q));
  Register #(.Bits(32)) USER_OUT (.D(Data_In), .C(CLK), .en(demultiplexer_1_out_3), .Q(USER_OUT_q));
  SoundDevice sounddevice_1 (.D(Data_In), .C(CLK), .E(demultiplexer_1_out_8), .Q(sounddevice_1_q));
  Register #(.Bits(32)) register_3 (.D(Data_In), .C(CLK), .en(demultiplexer_1_out_11), .Q(register_3_q));
  Register #(.Bits(32)) register_4 (.D(Data_In), .C(CLK), .en(demultiplexer_1_out_14), .Q(register_4_q));
  Register #(.Bits(32)) register_5 (.D(Data_In), .C(CLK), .en(demultiplexer_1_out_9), .Q(register_5_q));
  Register #(.Bits(32)) register_6 (.D(Data_In), .C(CLK), .en(demultiplexer_1_out_12), .Q(register_6_q));
  Register #(.Bits(32)) register_7 (.D(Data_In), .C(CLK), .en(demultiplexer_1_out_15), .Q(register_7_q));
  Multiplexer #(.Selector_Bits(4), .Bits(32)) multiplexer_1 (
    .sel(Addr[3:0]), .in_0(Stack_Top), .in_1({{16{1'b0}}, Stack_Pointer}), .in_2(keyboardbuffer_1_p5),
    .in_3(USER_OUT_q), .in_4(PC_In), .in_5(PD_In), .in_6(SUB_POINTER_q),
    .in_7({{31{1'b0}}, keyboardbuffer_1_p6[0]}), .in_8(sounddevice_1_q), .in_9(register_5_q),
    .in_10(register_1_q), .in_11(register_3_q), .in_12(register_6_q), .in_13(register_2_q),
    .in_14(register_4_q), .in_15(register_7_q), .out(multiplexer_1_out));
  Multiplexer #(.Bits(32)) multiplexer_2 (
    .sel(and_2_out), .in_0(multiplexer_1_out), .in_1(Subroutine_Stack_d), .out(multiplexer_2_out));
  assign Data = comparator_1_eq ? multiplexer_2_out : 32'bz;  // Driver driver_1

  assign New_Pointer = Data_In[15:0];

  // Notes on the sheet:
  //   MEMORY DEVICE 0
  //   Special Purpose Registers
endmodule
