// Digital circuit Device1.dig as structural Verilog
module Device1 (
  input  [31:0] Data_In,
  input  Push,
  input  Pop,
  input  CLK,
  input  [15:0] Addr,
  input  [5:0] Select,
  input  Write,
  input  [15:0] New_Pointer,
  input  Write_Pointer,
  output [31:0] Stack_Top,
  output [15:0] Stack_Pointer,
  output [31:0] Data
);

  wire and_1_out, comparator_1_eq;
  wire [31:0] mainstack_1_direct_read;

  Comparator #(.Bits(6)) comparator_1 (.a(Select), .b(6'b000001), .eq(comparator_1_eq));  // open: gt, lt
  and and_1 (and_1_out, comparator_1_eq, Write);
  MainStack mainstack_1 (
    .Data(Data_In), .Push(Push), .Pop(Pop), .Direct_Read_Address(Addr), .Direct_Write_Enable(and_1_out),
    .Direct_Write_Address(Addr), .New_Pointer(New_Pointer), .Write_Pointer(Write_Pointer), .CLK(CLK),
    .Top(Stack_Top), .Pointer(Stack_Pointer), .Direct_Read(mainstack_1_direct_read));
  assign Data = comparator_1_eq ? mainstack_1_direct_read : 32'bz;  // Driver driver_1

  // Notes on the sheet:
  //   MEMORY DEVICE 1
endmodule
