// Digital circuit Device4.dig as structural Verilog
module Device4 (
  input  CLK,
  input  [15:0] Addr,
  input  [5:0] Select,
  input  [31:0] Data_In,
  input  Write,
  output [31:0] Data
);

  wire and_1_out, comparator_1_eq, not_1_out;
  wire [15:0] graphiccard_1_d;

  Comparator #(.Bits(6)) comparator_1 (.a(Select), .b(6'b000100), .eq(comparator_1_eq));  // open: gt, lt
  and and_1 (and_1_out, comparator_1_eq, Write);
  not not_1 (not_1_out, and_1_out);
  GraphicCard #(.graphicHeight(256), .graphicWidth(256), .Bits(16)) graphiccard_1 (
    .A({1'b0, Addr}), .str(and_1_out), .C(CLK), .ld(not_1_out), .B(1'b0), .D(graphiccard_1_d));
  assign graphiccard_1_d = and_1_out ? Data_In[15:0] : 16'bz;  // Driver driver_1
  assign Data = comparator_1_eq ? {{16{1'b0}}, graphiccard_1_d} : 32'bz;  // Driver driver_2

  // Notes on the sheet:
  //   MEMORY DEVICE 4
endmodule
