// Digital circuit FetchUnit.dig as structural Verilog
module FetchUnit (
  input  CLK,
  input  Start,
  input  [5:0] PD,
  input  [15:0] PC,
  input  [31:0] Mem_In,
  output Start_Execute,
  output [5:0] Device,
  output [15:0] Addr,
  output [31:0] Instruction,
  output [31:0] Next_Line
);

  wire and_1_out, and_2_out, and_3_out, counter_1_ovf, or_1_out, or_2_out, xor_1_out;
  wire [1:0] counter_1_out;
  wire [15:0] add_1_s;

  Counter #(.Bits(2)) counter_1 (.en(or_1_out), .C(CLK), .clr(or_2_out), .out(counter_1_out), .ovf(counter_1_ovf));
  xor xor_1 (xor_1_out, counter_1_out[0], counter_1_out[1]);
  and and_1 (and_1_out, counter_1_out[0], counter_1_out[1]);
  or or_1 (or_1_out, xor_1_out, Start);
  or or_2 (or_2_out, and_1_out, counter_1_ovf);
  Add #(.Bits(16)) add_1 (.a(PC), .b({16{1'b0}}), .c_i(counter_1_out[1]), .s(add_1_s));  // open: c_o
  assign Device = or_1_out ? PD : 6'bz;  // Driver driver_1
  assign Addr = or_1_out ? add_1_s : 16'bz;  // Driver driver_2
  and and_2 (and_2_out, counter_1_out[0], ~counter_1_out[1]);  // And
  and and_3 (and_3_out, ~counter_1_out[0], counter_1_out[1]);  // And
  and and_4 (Start_Execute, counter_1_out[0], counter_1_out[1]);
  Register #(.Bits(32)) register_1 (.D(Mem_In), .C(CLK), .en(and_2_out), .Q(Instruction));
  Register #(.Bits(32)) register_2 (.D(Mem_In), .C(CLK), .en(and_3_out), .Q(Next_Line));
endmodule
