// Digital circuit KeyboardBuffer.dig as structural Verilog
module KeyboardBuffer (
  input  CLK,
  input  [3:0] ADDR,
  input  SEL,
  input  EN,
  output Av,
  output [31:0] Char
);

  wire comparator_1_eq, d_ff_1_q, nand_1_out;
  wire [0:0] and_1_out, comparator_2_gt;
  wire [15:0] add_1_s, add_2_s, d_ff_2_q, d_ff_3_q, d_ff_4_q, keyboard_1_d, sub_1_s;

  Comparator #(.Bits(4)) comparator_1 (.a(ADDR), .b(4'b0010), .eq(comparator_1_eq));  // open: gt, lt
  nand nand_1 (nand_1_out, comparator_1_eq, SEL);
  Keyboard keyboard_1 (.C(CLK), .en(nand_1_out), .D(keyboard_1_d));  // open: av
  PullDown #(.Bits(16)) pulldown_1 (.out(keyboard_1_d));
  Comparator #(.Bits(16)) comparator_2 (.a(keyboard_1_d), .b({16{1'b0}}), .gt(comparator_2_gt[0]));  // open: eq, lt
  and and_1 (and_1_out[0], EN, Av);
  Add #(.Bits(16)) add_1 (.a({{15{1'b0}}, comparator_2_gt[0]}), .b(d_ff_2_q), .c_i(1'b0), .s(add_1_s));  // open: c_o
  Add #(.Bits(16)) add_2 (.a({{15{1'b0}}, and_1_out[0]}), .b(d_ff_4_q), .c_i(1'b0), .s(add_2_s));  // open: c_o
  D_FF d_ff_1 (.D(comparator_2_gt[0]), .C(~CLK), .Q(d_ff_1_q));  // open: nQ
  D_FF #(.Bits(16)) d_ff_2 (.D(add_1_s), .C(CLK), .Q(d_ff_2_q));  // open: nQ
  D_FF #(.Bits(16)) d_ff_3 (.D(keyboard_1_d), .C(~CLK), .Q(d_ff_3_q));  // open: nQ
  D_FF #(.Bits(16)) d_ff_4 (.D(add_2_s), .C(CLK), .Q(d_ff_4_q));  // open: nQ
  RAMDualAccess #(.AddrBits(16), .Bits(16)) ramdualaccess_1 (
    .str(d_ff_1_q), .C(CLK), .ld(1'b1), .A1(d_ff_2_q), .Din1(d_ff_3_q), .A2(d_ff_4_q), .D2(Char[15:0]));  // open: D1
  Sub #(.Bits(16)) sub_1 (.a(d_ff_2_q), .b(d_ff_4_q), .c_i(1'b0), .s(sub_1_s));  // open: c_o
  Comparator #(.Bits(16)) comparator_3 (.a(sub_1_s), .b({16{1'b0}}), .gt(Av));  // open: eq, lt
  // Pins of 1 and 32 bits meet at {{16{1'b0}}, Char[15:0]}

  assign Char[31:16] = {16{1'b0}};
endmodule
