// Digital circuit NextState.dig as structural Verilog
module NextState (
  input  Start_Execute,
  input  [31:0] Instruction,
  input  [15:0] Prev__State,
  input  [15:0] Branch_Loc,
  input  [2:0] Branch_Cond,
  input  [2:0] PZN,
  output [15:0] Next_State
);

  wire and_1_out, and_2_out, and_3_out, or_1_out;
  wire [15:0] add_1_s, add_2_s, barrelshifter_1_out, multiplexer_1_out;

  Add #(.Bits(16)) add_1 (.a(16'h1), .b(Prev__State), .c_i(1'b0), .s(add_1_s));  // open: c_o
  and and_1 (and_1_out, Branch_Cond[0], PZN[0]);
  and and_2 (and_2_out, Branch_Cond[1], PZN[1]);
  and and_3 (and_3_out, Branch_Cond[2], PZN[2]);
  Add #(.Bits(16)) add_2 (.a(Instruction[15:0]), .b(16'h1), .c_i(1'b0), .s(add_2_s));  // open: c_o
  or or_1 (or_1_out, and_1_out, and_2_out, and_3_out);
  Multiplexer #(.Bits(16)) multiplexer_1 (.sel(or_1_out), .in_0(add_1_s), .in_1(Branch_Loc), .out(multiplexer_1_out));
  BarrelShifter #(.Bits(16)) barrelshifter_1 (.in(add_2_s), .shift(5'b00100), .out(barrelshifter_1_out));
  Multiplexer #(.Bits(16)) multiplexer_2 (
    .sel(Start_Execute), .in_0(multiplexer_1_out), .in_1(barrelshifter_1_out), .out(Next_State));
endmodule
