// Digital circuit SoundDevice.dig as structural Verilog
module SoundDevice (
  input  [31:0] D,
  input  C,
  input  E,
  output [31:0] Q
);

  wire and_1_out, and_2_out, and_3_out, and_4_out, comparator_1_eq, comparator_2_eq, comparator_3_eq,
       comparator_4_eq, delay_1_out, multiplexer_2_out, multiplexer_3_out, O1, O2, or_1_out, or_3_out, PC1,
       PC2, reset_1_out, reset_2_out, reset_3_out;
  wire [6:0] multiplexer_1_out, multiplexer_1_out_3, multiplexer_4_out, multiplexer_5_out, multiplexer_6_out,
       multiplexer_7_out, register_2_q, register_3_q, register_4_q, register_5_q;
  wire [31:8] multiplexer_1_out_2;

  Reset #(.invertOutput("false")) reset_1 (.out(reset_1_out));
  Reset #(.invertOutput("false")) reset_2 (.out(reset_2_out));
  Reset #(.invertOutput("false")) reset_3 (.out(reset_3_out));
  Multiplexer #(.Bits(32)) multiplexer_1 (
    .sel(reset_1_out), .in_0(D), .in_1(32'h30003000),
    .out({multiplexer_1_out_2[31:24], PC2, multiplexer_1_out_3, multiplexer_1_out_2[15:8], PC1, multiplexer_1_out}));
  Multiplexer multiplexer_2 (.sel(delay_1_out), .in_0(C), .in_1(1'b1), .out(multiplexer_2_out));
  Delay #(.delayTime(4)) delay_1 (.in(reset_2_out), .out(delay_1_out));
  Multiplexer multiplexer_3 (.sel(reset_3_out), .in_0(E), .in_1(1'b1), .out(multiplexer_3_out));
  Comparator #(.Bits(7)) comparator_1 (
    .a({7{1'b0}}), .b(multiplexer_1_out_2[14:8]), .eq(comparator_1_eq));  // open: gt, lt
  Comparator #(.Bits(7)) comparator_2 (.a({7{1'b0}}), .b(multiplexer_1_out), .eq(comparator_2_eq));  // open: gt, lt
  Comparator #(.Bits(7)) comparator_3 (
    .a({7{1'b0}}), .b(multiplexer_1_out_2[30:24]), .eq(comparator_3_eq));  // open: gt, lt
  Comparator #(.Bits(7)) comparator_4 (.a({7{1'b0}}), .b(multiplexer_1_out_3), .eq(comparator_4_eq));  // open: gt, lt
  or or_1 (or_1_out, multiplexer_1_out_2[15], ~comparator_1_eq);  // Or
  or or_2 (O1, PC1, ~comparator_2_eq);  // Or
  or or_3 (or_3_out, multiplexer_1_out_2[31], ~comparator_3_eq);  // Or
  or or_4 (O2, PC2, ~comparator_4_eq);  // Or
  and and_1 (and_1_out, or_1_out, multiplexer_3_out);
  and and_2 (and_2_out, O1, multiplexer_3_out);
  and and_3 (and_3_out, or_3_out, multiplexer_3_out);
  and and_4 (and_4_out, O2, multiplexer_3_out);
  Register #(.Bits(32)) register_1 (
    .D({multiplexer_1_out_2[31:24], PC2, multiplexer_1_out_3, multiplexer_1_out_2[15:8], PC1, multiplexer_1_out}),
    .C(multiplexer_2_out), .en(multiplexer_3_out), .Q(Q));
  Register #(.Bits(7)) register_2 (
    .D(multiplexer_1_out_2[14:8]), .C(multiplexer_2_out), .en(and_1_out), .Q(register_2_q));
  Register #(.Bits(7)) register_3 (.D(multiplexer_1_out), .C(multiplexer_2_out), .en(and_2_out), .Q(register_3_q));
  Register #(.Bits(7)) register_4 (
    .D(multiplexer_1_out_2[30:24]), .C(multiplexer_2_out), .en(and_3_out), .Q(register_4_q));
  Register #(.Bits(7)) register_5 (.D(multiplexer_1_out_3), .C(multiplexer_2_out), .en(and_4_out), .Q(register_5_q));
  Multiplexer #(.Bits(7)) multiplexer_4 (
    .sel(and_1_out), .in_0(register_2_q), .in_1(multiplexer_1_out_2[14:8]), .out(multiplexer_4_out));
  Multiplexer #(.Bits(7)) multiplexer_5 (
    .sel(and_2_out), .in_0(register_3_q), .in_1(multiplexer_1_out), .out(multiplexer_5_out));
  Multiplexer #(.Bits(7)) multiplexer_6 (
    .sel(and_3_out), .in_0(register_4_q), .in_1(multiplexer_1_out_2[30:24]), .out(multiplexer_6_out));
  Multiplexer #(.Bits(7)) multiplexer_7 (
    .sel(and_4_out), .in_0(register_5_q), .in_1(multiplexer_1_out_3), .out(multiplexer_7_out));
  // MIDI #(.midiProgChange("true"), .midiInstrument("Lead 1 (square)")) Channel_1: pin names not known; wires that end beside it: multiplexer_5_out, multiplexer_4_out, O1, PC1, multiplexer_3_out, multiplexer_2_out
  // MIDI #(.midiProgChange("true"), .midiInstrument("Lead 1 (square)"), .midiChannel(2)) Channel_2: pin names not known; wires that end beside it: multiplexer_7_out, multiplexer_6_out, O2, PC2, multiplexer_3_out, multiplexer_2_out
endmodule
