// Digital circuit ControlUnit.dig as structural Verilog
module ControlUnit (
  input  clk
);

  wire [15:0] counter_1_out;
  wire [63:0] rom_1_d;

  Counter #(.Bits(16)) counter_1 (.en(1'b1), .C(clk), .clr(1'b0), .out(counter_1_out));  // open: ovf
  ROM #(.AddrBits(16), .isProgramMemory("true"), .Bits(64)) rom_1 (.A(counter_1_out), .sel(1'b1), .D(rom_1_d));
  // Probe on counter_1_out
  // Probe on rom_1_d
endmodule
