// Digital circuit Datapath.dig as structural Verilog
module Datapath (
  input  [27:0] ControlWord,
  input  [31:0] ConstIn,
  input  [31:0] NextLine,
  input  CLK,
  input  [31:0] MemIn,
  input  [31:0] StackTop,
  output [31:0] Push_Out,
  output Push_Enable,
  output [31:0] Mem_Out,
  output Mem_Write,
  output [5:0] Device_Select,
  output Pop_Enable,
  output [31:0] Mem_Addr,
  output [2:0] PZN
);

  wire and_1_out, driver_2_out, driver_4_out, driver_8_out, driver_9_out, driver_10_out, driver_11_out;
  wire [1:0] driver_7_out;
  wire [2:0] comparator_1_gt, driver_1_out, driver_3_out, driver_5_out;
  wire [3:0] driver_6_out;
  wire [5:0] driver_12_out, multiplexer_2_out, multiplexer_3_out, register_1_q;
  wire [31:0] alu_1_result, driver_13_out, driver_14_out, driver_15_out, driver_16_out, multiplexer_1_out,
       registerfile_1_da, registerfile_1_db;
  wire [31:6] multiplexer_2_out_2;

  assign driver_1_out = ControlWord[27] ? ControlWord[26:24] : 3'bz;  // Driver driver_1
  assign driver_2_out = ControlWord[27] ? ControlWord[23] : 1'bz;  // Driver driver_2
  assign driver_3_out = ControlWord[27] ? ControlWord[22:20] : 3'bz;  // Driver driver_3
  assign driver_4_out = ControlWord[27] ? ControlWord[19] : 1'bz;  // Driver driver_4
  assign driver_5_out = ControlWord[27] ? ControlWord[18:16] : 3'bz;  // Driver driver_5
  assign driver_6_out = ControlWord[27] ? ControlWord[15:12] : 4'bz;  // Driver driver_6
  assign driver_7_out = ControlWord[27] ? ControlWord[11:10] : 2'bz;  // Driver driver_7
  assign driver_8_out = ControlWord[27] ? ControlWord[9] : 1'bz;  // Driver driver_8
  assign driver_9_out = ControlWord[27] ? ControlWord[8] : 1'bz;  // Driver driver_9
  assign driver_10_out = ControlWord[27] ? ControlWord[7] : 1'bz;  // Driver driver_10
  assign driver_11_out = ControlWord[27] ? ControlWord[6] : 1'bz;  // Driver driver_11
  assign driver_12_out = ControlWord[27] ? ControlWord[5:0] : 6'bz;  // Driver driver_12
  assign driver_13_out = ControlWord[27] ? ConstIn : 32'bz;  // Driver driver_13
  assign driver_14_out = ControlWord[27] ? NextLine : 32'bz;  // Driver driver_14
  assign driver_15_out = ControlWord[27] ? MemIn : 32'bz;  // Driver driver_15
  assign driver_16_out = ControlWord[27] ? StackTop : 32'bz;  // Driver driver_16
  PullDown #(.Bits(3)) pulldown_1 (.out(driver_1_out));
  PullDown pulldown_2 (.out(driver_2_out));
  PullDown #(.Bits(3)) pulldown_3 (.out(driver_3_out));
  PullDown pulldown_4 (.out(driver_4_out));
  PullDown #(.Bits(32)) pulldown_5 (.out(driver_13_out));
  PullDown #(.Bits(32)) pulldown_6 (.out(driver_14_out));
  PullDown #(.Bits(32)) pulldown_7 (.out(driver_15_out));
  PullDown #(.Bits(32)) pulldown_8 (.out(driver_16_out));
  RegisterFile #(.AddrBits(3), .Bits(32)) registerfile_1 (
    .Din({multiplexer_2_out_2, multiplexer_2_out}), .we(driver_4_out), .Rw(driver_5_out), .C(CLK),
    .Ra(driver_1_out), .Rb(driver_3_out), .Da(registerfile_1_da), .Db(registerfile_1_db));
  PullDown #(.Bits(3)) pulldown_9 (.out(driver_5_out));
  PullDown #(.Bits(4)) pulldown_10 (.out(driver_6_out));
  PullDown #(.Bits(2)) pulldown_11 (.out(driver_7_out));
  PullDown pulldown_12 (.out(driver_8_out));
  PullDown pulldown_13 (.out(driver_9_out));
  PullDown pulldown_14 (.out(driver_10_out));
  PullDown pulldown_15 (.out(driver_11_out));
  PullDown #(.Bits(6)) pulldown_16 (.out(driver_12_out));
  Multiplexer #(.Bits(32)) multiplexer_1 (
    .sel(driver_2_out), .in_0(registerfile_1_db), .in_1(driver_13_out), .out(multiplexer_1_out));
  ALU alu_1 (.A(registerfile_1_da), .B(multiplexer_1_out), .F(driver_6_out), .Result(alu_1_result));
  and and_1 (and_1_out, driver_7_out[0], driver_7_out[1]);
  Multiplexer #(.Selector_Bits(2), .Bits(32)) multiplexer_2 (
    .sel(driver_7_out), .in_0(alu_1_result), .in_1(driver_14_out), .in_2(driver_15_out),
    .in_3(driver_16_out), .out({multiplexer_2_out_2, multiplexer_2_out}));
  Register #(.Bits(6)) register_1 (.D(multiplexer_2_out), .C(CLK), .en(driver_11_out), .Q(register_1_q));
  Comparator #(.Bits(32)) comparator_1 (
    .a({multiplexer_2_out_2, multiplexer_2_out}), .b({32{1'b0}}), .gt(comparator_1_gt[2]),
    .eq(comparator_1_gt[1]), .lt(comparator_1_gt[0]));
  Multiplexer #(.Bits(6)) multiplexer_3 (
    .sel(driver_10_out), .in_0(register_1_q), .in_1(driver_12_out), .out(multiplexer_3_out));
  Multiplexer #(.Bits(3)) multiplexer_4 (.sel(ControlWord[27]), .in_0(3'b000), .in_1(comparator_1_gt), .out(PZN));
  assign Push_Out = ControlWord[27] ? {multiplexer_2_out_2, multiplexer_2_out} : 32'bz;  // Driver driver_17
  assign Push_Enable = ControlWord[27] ? driver_8_out : 1'bz;  // Driver driver_18
  assign Mem_Out = ControlWord[27] ? {multiplexer_2_out_2, multiplexer_2_out} : 32'bz;  // Driver driver_19
  assign Mem_Write = ControlWord[27] ? driver_9_out : 1'bz;  // Driver driver_20
  assign Pop_Enable = ControlWord[27] ? and_1_out : 1'bz;  // Driver driver_21
  assign Mem_Addr = ControlWord[27] ? multiplexer_1_out : 32'bz;  // Driver driver_22
  assign Device_Select = ControlWord[27] ? multiplexer_3_out : 6'bz;  // Driver driver_23

  // Notes on the sheet:
  //   Enable
  //   A Addr
  //   Const Select
  //   B Addr
  //   D Write
  //   D Addr
  //   Function
  //   Result Select
  //   Push Result
  //   Store Result
  //   Dev Select
  //   Dev Write
  //   Dev Const
endmodule
