// Digital circuit MainStack.dig as structural Verilog
module MainStack (
  input  [31:0] Data,
  input  Push,
  input  Pop,
  input  [15:0] Direct_Read_Address,
  input  Direct_Write_Enable,
  input  [15:0] Direct_Write_Address,
  input  [15:0] New_Pointer,
  input  Write_Pointer,
  input  CLK,
  output [31:0] Top,
  output [15:0] Pointer,
  output [31:0] Direct_Read
);

  wire or_1_out;
  wire [15:0] multiplexer_1_out;

  StackPointer stackpointer_1 (
    .Write(Write_Pointer), .Subtract(Pop), .Stable(Direct_Write_Enable), .Add(Push),
    .Write_Data(New_Pointer), .CLK(CLK), .Data(Pointer));
  Multiplexer #(.Bits(16)) multiplexer_1 (
    .sel(Direct_Write_Enable), .in_0(Pointer), .in_1(Direct_Write_Address), .out(multiplexer_1_out));
  or or_1 (or_1_out, Push, Direct_Write_Enable);
  RegisterFile #(.AddrBits(16), .Bits(32)) registerfile_1 (
    .Din(Data), .we(or_1_out), .Rw(multiplexer_1_out), .C(CLK), .Ra(Pointer), .Rb(Direct_Read_Address),
    .Da(Top), .Db(Direct_Read));

  // Notes on the sheet:
  //   Data: Data to be written to stack, either by pushing or direct writing.
  //   Push: Pushes the value given at data onto the stack.
  //   Pop: Pops the uppermost value off of the stack.
  //   Direct_Read_Address: Used to read data from an arbetrary address of the stack. 
  //   Note that when a value is popped from the stack, it will remain in
  //   place until overwritten....
  //   Direct_Write_Address: Used to write Data directly to a certain part of the stack
  //   New_Pointer: Resets the stack pointer to the specified value when write pointer is asserted.
  //   Write_Pointer: When asserted, the value given at New Pointer will be pushed to the stack pointer register.
endmodule
