// Digital circuit SID.dig as structural Verilog
module SID (
  input  [63:0] Instr,
  input  [15:0] PC,
  input  [15:0] B,
  input  [2:0] B_2,
  input  [2:0] PZN,
  output [15:0] Loc,
  output [2:0] Cond,
  output [2:0] PZN_2,
  output [15:0] PC_2
);

  wire comparator_1_eq, comparator_2_eq, comparator_3_eq, or_1_out;
  wire [1:0] priorityencoder_1_num;

  Comparator #(.Bits(64)) comparator_1 (.a(Instr), .b({64{1'b0}}), .eq(comparator_1_eq));  // open: gt, lt
  Comparator #(.Bits(64)) comparator_2 (.a(Instr), .b(64'h1), .eq(comparator_2_eq));  // open: gt, lt
  Comparator #(.Bits(64)) comparator_3 (.a(Instr), .b(64'h2), .eq(comparator_3_eq));  // open: gt, lt
  or or_1 (or_1_out, comparator_1_eq, comparator_2_eq, comparator_3_eq);
  PriorityEncoder #(.Selector_Bits(2)) priorityencoder_1 (
    .in0(comparator_1_eq), .in1(comparator_2_eq), .in2(comparator_3_eq), .in3(1'b0),
    .num(priorityencoder_1_num));  // open: any
  Multiplexer #(.Bits(16)) multiplexer_1 (.sel(or_1_out), .in_0(B), .in_1({16{1'b0}}), .out(Loc));
  Multiplexer #(.Bits(3)) multiplexer_2 (.sel(or_1_out), .in_0(B_2), .in_1(3'b010), .out(Cond));
  Multiplexer #(.Bits(3)) multiplexer_3 (.sel(or_1_out), .in_0(PZN), .in_1(3'b010), .out(PZN_2));
  Add #(.Bits(16)) add_1 (.a({{14{1'b0}}, priorityencoder_1_num}), .b(PC), .c_i(1'b0), .s(PC_2));  // open: c_o
endmodule
