// Digital circuit StackPointer.dig as structural Verilog
module StackPointer (
  input  Write,
  input  Subtract,
  input  Stable,
  input  Add,
  input  [15:0] Write_Data,
  input  CLK,
  output [15:0] Data
);

  wire not_1_out, priorityencoder_1_any;
  wire [1:0] multiplexer_2_out, priorityencoder_1_num;
  wire [15:0] add_1_s, multiplexer_1_out, multiplexer_3_out, register_1_q, sub_1_s;

  PriorityEncoder #(.Selector_Bits(2)) priorityencoder_1 (
    .in0(Write), .in1(Subtract), .in2(Add), .in3(Stable), .num(priorityencoder_1_num),
    .any(priorityencoder_1_any));
  Sub #(.Bits(16)) sub_1 (.a(register_1_q), .b(16'h1), .c_i(1'b0), .s(sub_1_s));  // open: c_o
  Add #(.Bits(16)) add_1 (.a(register_1_q), .b(16'h1), .c_i(1'b0), .s(add_1_s));  // open: c_o
  Multiplexer #(.Selector_Bits(2), .Bits(16)) multiplexer_1 (
    .sel(multiplexer_2_out), .in_0(Write_Data), .in_1(sub_1_s), .in_2(add_1_s), .in_3(register_1_q),
    .out(multiplexer_1_out));
  Multiplexer #(.Bits(2)) multiplexer_2 (
    .sel(priorityencoder_1_any), .in_0(2'b11), .in_1(priorityencoder_1_num), .out(multiplexer_2_out));
  not not_1 (not_1_out, CLK);
  Register #(.Bits(16)) register_1 (.D(multiplexer_1_out), .C(not_1_out), .en(priorityencoder_1_any), .Q(register_1_q));
  Multiplexer #(.Bits(16)) multiplexer_3 (
    .sel(Subtract), .in_0(multiplexer_1_out), .in_1(register_1_q), .out(multiplexer_3_out));
  Sub #(.Bits(16)) sub_2 (.a(multiplexer_3_out), .b(16'h1), .c_i(1'b0), .s(Data));  // open: c_o
endmodule
